// Digital circuit ADD12_MSB.dig as structural Verilog
module ADD12_MSB (
  input  [11:0] B,
  input  [11:0] A,
  input  C_in,
  output C_out,
  output [11:0] S
);

  wire fadder_1_p1, fadder_2_p1, fadder_3_p1, fadder_4_p1, fadder_5_p1, fadder_6_p1, fadder_7_p1,
       fadder_8_p1, fadder_9_p1, fadder_10_p1, fadder_11_p1;

  // fAdder fadder_1: pin names not known; wires that end beside it: fadder_1_p1, A[11], C_out, B[11], S[11]
  // fAdder fadder_2: pin names not known; wires that end beside it: fadder_2_p1, A[10], fadder_1_p1, B[10], S[10]
  // fAdder fadder_3: pin names not known; wires that end beside it: fadder_3_p1, A[9], fadder_2_p1, B[9], S[9]
  // fAdder fadder_4: pin names not known; wires that end beside it: fadder_4_p1, A[8], fadder_3_p1, B[8], S[8]
  // fAdder fadder_5: pin names not known; wires that end beside it: fadder_5_p1, A[7], fadder_4_p1, B[7], S[7]
  // fAdder fadder_6: pin names not known; wires that end beside it: fadder_6_p1, A[6], fadder_5_p1, B[6], S[6]
  // fAdder fadder_7: pin names not known; wires that end beside it: fadder_7_p1, A[5], fadder_6_p1, B[5], S[5]
  // fAdder fadder_8: pin names not known; wires that end beside it: fadder_8_p1, A[4], fadder_7_p1, B[4], S[4]
  // fAdder fadder_9: pin names not known; wires that end beside it: fadder_9_p1, A[3], fadder_8_p1, B[3], S[3]
  // fAdder fadder_10: pin names not known; wires that end beside it: fadder_10_p1, A[2], fadder_9_p1, B[2], S[2]
  // fAdder fadder_11: pin names not known; wires that end beside it: fadder_11_p1, A[1], fadder_10_p1, B[1], S[1]
  // fAdder fadder_12: pin names not known; wires that end beside it: C_in, A[0], fadder_11_p1, B[0], S[0]
endmodule
