// Digital circuit ADD24.dig as structural Verilog
module ADD24 (
  input  [23:0] A,
  input  [23:0] B,
  output [23:0] S
);

  wire add12_lsb_1_c_out;
  wire [11:0] add12_msb_1_s, add12_msb_2_s;

  ADD12_LSB add12_lsb_1 (.B(B[11:0]), .A(A[11:0]), .S(S[11:0]), .C_out(add12_lsb_1_c_out));
  ADD12_MSB add12_msb_1 (.B(B[23:12]), .A(A[23:12]), .C_in(1'b0), .S(add12_msb_1_s));  // open: C_out
  ADD12_MSB add12_msb_2 (.B(B[23:12]), .A(A[23:12]), .C_in(1'b1), .S(add12_msb_2_s));  // open: C_out
  Multiplexer #(.Bits(12)) multiplexer_1 (
    .sel(add12_lsb_1_c_out), .in_0(add12_msb_1_s), .in_1(add12_msb_2_s), .out(S[23:12]));
endmodule
