// Digital circuit CONTROL_MEM.dig as structural Verilog
module CONTROL_MEM (
  input  [3:0] OPCODE,
  output [8:0] S
);

  ROM #(.AddrBits(4), .Bits(9)) rom_1 (.A(OPCODE), .sel(1'b1), .D(S));

  // Notes on the sheet:
  //   contents of rom_1 (hex, n*v repeats v):
  //   0,20,24,28,2c,30,34,38,3c,2e,32,22,1,80,104,40
endmodule
