// Digital circuit CPU.dig as structural Verilog
module CPU (
  input  CLK,
  output [31:0] DISPLAY
);

  wire and_1_out, D_EN, IP_plus_0, IP_plus_BEQ, IP_plus_JMP, REG_WRITE, ULA_MUX, ZERO;
  wire [2:0] ULA_FUN;
  wire [3:0] a, b, c;
  wire [15:0] \const ;
  wire [23:0] add24_1_s, add24_2_s, IP_s, multiplexer_1_out, multiplexer_2_out, multiplexer_3_out,
       SIGN_EXT_24_s;
  wire [31:0] multiplexer_4_out, REG_BANK_a_2, REG_BANK_b_2, SIGN_EXT_32_s, ULA_p4;
  wire [31:28] PROG_MEM_d;

  EXT_24 SIGN_EXT_24 (.CONST(\const ), .S(SIGN_EXT_24_s));
  ADD24 add24_1 (.A(24'h1), .B(IP_s), .S(add24_1_s));
  ADD24 add24_2 (.A(IP_s), .B(SIGN_EXT_24_s), .S(add24_2_s));
  Multiplexer #(.Bits(24)) multiplexer_1 (.sel(IP_plus_0), .in_0(add24_1_s), .in_1(IP_s), .out(multiplexer_1_out));
  REG_BANK REG_BANK (
    .W(ULA_p4), .c(c), .a(a), .CLK(CLK), .b(b), .REG_W(REG_WRITE), .A_2(REG_BANK_a_2), .B_2(REG_BANK_b_2));
  EXT_32 SIGN_EXT_32 (.CONST(\const ), .S(SIGN_EXT_32_s));
  Multiplexer #(.Bits(24)) multiplexer_2 (
    .sel(IP_plus_JMP), .in_0(multiplexer_1_out), .in_1(add24_2_s), .out(multiplexer_2_out));
  Multiplexer #(.Bits(24)) multiplexer_3 (
    .sel(and_1_out), .in_0(multiplexer_2_out), .in_1(add24_2_s), .out(multiplexer_3_out));
  and and_1 (and_1_out, IP_plus_BEQ, ZERO);
  Multiplexer #(.Bits(32)) multiplexer_4 (
    .sel(ULA_MUX), .in_0(REG_BANK_b_2), .in_1(SIGN_EXT_32_s), .out(multiplexer_4_out));
  IP IP (.CLK(CLK), .A(multiplexer_3_out), .S(IP_s));
  Multiplexer #(.Bits(32)) multiplexer_5 (.sel(D_EN), .in_0({32{1'b1}}), .in_1(REG_BANK_a_2), .out(DISPLAY));
  PROGRAM_MEM PROG_MEM (.A(IP_s), .D({PROG_MEM_d, a, b, c, \const }));
  // ULA ULA: pin names not known; wires that end beside it: REG_BANK_a_2, multiplexer_4_out, ULA_FUN, ULA_p4, ZERO
  CONTROL_MEM CTRL_MEM (
    .OPCODE(PROG_MEM_d), .S({IP_plus_BEQ, IP_plus_JMP, IP_plus_0, REG_WRITE, ULA_FUN, ULA_MUX, D_EN}));

  // Notes on the sheet:
  //   CLK: Hz: 2
endmodule
