// Digital circuit PROGRAM_MEM.dig as structural Verilog
module PROGRAM_MEM (
  input  [23:0] A,
  output [31:0] D
);

  ROM #(.AddrBits(24), .Bits(32)) rom_1 (.A(A), .sel(1'b1), .D(D));

  // Notes on the sheet:
  //   contents of rom_1 (hex, n*v repeats v):
  //   0,b0010000,b0020001,b003000f,c3000000,b0040000,11250000,c5000000
  //   ,12010000,15020000,b4040001,e3400002,d000fffa,f0000000
endmodule
