// Digital circuit REG_BANK.dig as structural Verilog
module REG_BANK (
  input  [31:0] W,
  input  [3:0] c,
  input  [3:0] a,
  input  CLK,
  input  [3:0] b,
  input  REG_W,
  output [31:0] A_2,
  output [31:0] B_2
);

  wire and_1_out, and_2_out, and_3_out, and_4_out, and_5_out, and_6_out, and_7_out, and_8_out, and_9_out,
       and_10_out, and_11_out, and_12_out, and_13_out, and_14_out, and_15_out, and_16_out, E_0, E_1, E_2,
       E_3, E_4, E_5, E_6, E_7, E_8, E_9, E_10, E_11, E_12, E_13, E_14, E_15;
  wire [31:0] and_17_out, and_18_out, R_0, R_1, R_2, R_3, R_4, R_5, R_6, R_7, R_8, R_9, R_10, R_11, R_12,
       R_13, R_14, R_15, W_0, W_1, W_2, W_3, W_4, W_5, W_6, W_7, W_8, W_9, W_10, W_11, W_12, W_13, W_14, W_15;

  Demultiplexer #(.Selector_Bits(4), .Bits(32)) demultiplexer_1 (
    .sel(c), .in(W), .out_0(W_0), .out_1(W_1), .out_2(W_2), .out_3(W_3), .out_4(W_4), .out_5(W_5),
    .out_6(W_6), .out_7(W_7), .out_8(W_8), .out_9(W_9), .out_10(W_10), .out_11(W_11), .out_12(W_12),
    .out_13(W_13), .out_14(W_14), .out_15(W_15));
  Decoder #(.Selector_Bits(4)) decoder_1 (
    .sel(c), .out_0(E_0), .out_1(E_1), .out_2(E_2), .out_3(E_3), .out_4(E_4), .out_5(E_5), .out_6(E_6),
    .out_7(E_7), .out_8(E_8), .out_9(E_9), .out_10(E_10), .out_11(E_11), .out_12(E_12), .out_13(E_13),
    .out_14(E_14), .out_15(E_15));
  and and_1 (and_1_out, REG_W, E_0);
  and and_2 (and_2_out, REG_W, E_1);
  and and_3 (and_3_out, REG_W, E_2);
  and and_4 (and_4_out, REG_W, E_3);
  and and_5 (and_5_out, REG_W, E_4);
  and and_6 (and_6_out, REG_W, E_5);
  and and_7 (and_7_out, REG_W, E_6);
  and and_8 (and_8_out, REG_W, E_7);
  and and_9 (and_9_out, REG_W, E_8);
  and and_10 (and_10_out, REG_W, E_9);
  and and_11 (and_11_out, REG_W, E_10);
  and and_12 (and_12_out, REG_W, E_11);
  and and_13 (and_13_out, REG_W, E_12);
  and and_14 (and_14_out, REG_W, E_13);
  and and_15 (and_15_out, REG_W, E_14);
  and and_16 (and_16_out, REG_W, E_15);
  // REG reg_1: pin names not known; wires that end beside it: W_0, CLK, and_1_out, R_0
  // REG reg_2: pin names not known; wires that end beside it: W_1, CLK, and_2_out, R_1
  // REG reg_3: pin names not known; wires that end beside it: W_2, CLK, and_3_out, R_2
  // REG reg_4: pin names not known; wires that end beside it: W_3, CLK, and_4_out, R_3
  // REG reg_5: pin names not known; wires that end beside it: W_4, CLK, and_5_out, R_4
  // REG reg_6: pin names not known; wires that end beside it: W_5, CLK, and_6_out, R_5
  // REG reg_7: pin names not known; wires that end beside it: W_6, CLK, and_7_out, R_6
  // REG reg_8: pin names not known; wires that end beside it: W_7, CLK, and_8_out, R_7
  // REG reg_9: pin names not known; wires that end beside it: W_8, CLK, and_9_out, R_8
  // REG reg_10: pin names not known; wires that end beside it: W_9, CLK, and_10_out, R_9
  // REG reg_11: pin names not known; wires that end beside it: W_10, CLK, and_11_out, R_10
  // REG reg_12: pin names not known; wires that end beside it: W_11, CLK, and_12_out, R_11
  // REG reg_13: pin names not known; wires that end beside it: W_12, CLK, and_13_out, R_12
  // REG reg_14: pin names not known; wires that end beside it: W_13, CLK, and_14_out, R_13
  // REG reg_15: pin names not known; wires that end beside it: W_14, CLK, and_15_out, R_14
  // REG reg_16: pin names not known; wires that end beside it: W_15, CLK, and_16_out, R_15
  assign and_17_out = {32{1'b0}} & R_0;  // And and_17, 32 bits wide
  assign and_18_out = {32{1'b0}} & R_0;  // And and_18, 32 bits wide
  Multiplexer #(.Selector_Bits(4), .Bits(32)) multiplexer_1 (
    .sel(a), .in_0(and_17_out), .in_1(R_1), .in_2(R_2), .in_3(R_3), .in_4(R_4), .in_5(R_5), .in_6(R_6),
    .in_7(R_7), .in_8(R_8), .in_9(R_9), .in_10(R_10), .in_11(R_11), .in_12(R_12), .in_13(R_13), .in_14(R_14),
    .in_15(R_15), .out(A_2));
  Multiplexer #(.Selector_Bits(4), .Bits(32)) multiplexer_2 (
    .sel(b), .in_0(and_18_out), .in_1(R_1), .in_2(R_2), .in_3(R_3), .in_4(R_4), .in_5(R_5), .in_6(R_6),
    .in_7(R_7), .in_8(R_8), .in_9(R_9), .in_10(R_10), .in_11(R_11), .in_12(R_12), .in_13(R_13), .in_14(R_14),
    .in_15(R_15), .out(B_2));

  // Notes on the sheet:
  //   CLK: Hz: 5
endmodule
