// Digital circuit C2.dig as structural Verilog
module C2 (
  input  [31:0] B,
  output [31:0] S
);

  wire add16_lsb_1_p4, add16_msb_1_p4, add16_msb_2_p4;
  wire [15:0] add16_msb_1_p5, add16_msb_2_p5, not_1_out, not_1_out_2;

  assign {not_1_out_2, not_1_out} = ~B;  // Not not_1, 32 bits wide
  // ADD16_LSB add16_lsb_1: pin names not known; wires that end beside it: not_1_out, S[15:0], 16'h1, add16_lsb_1_p4
  // ADD16_MSB add16_msb_1: pin names not known; wires that end beside it: {16{1'b0}}, not_1_out_2, 1'b0, add16_msb_1_p4, add16_msb_1_p5
  // ADD16_MSB add16_msb_2: pin names not known; wires that end beside it: {16{1'b0}}, not_1_out_2, 1'b1, add16_msb_2_p4, add16_msb_2_p5
  LED led_1 (.in(add16_msb_1_p4));
  LED led_2 (.in(add16_msb_2_p4));
  Multiplexer #(.Bits(16)) multiplexer_1 (
    .sel(add16_lsb_1_p4), .in_0(add16_msb_1_p5), .in_1(add16_msb_2_p5), .out(S[31:16]));
endmodule
