// Digital circuit SUB.dig as structural Verilog
module SUB (
  input  [31:0] A,
  input  [31:0] B,
  output [31:0] S
);

  wire add16_lsb_1_p4, add16_msb_1_p4, add16_msb_2_p4;
  wire [15:0] add16_msb_1_p5, add16_msb_2_p5;
  wire [31:0] c2_1_s;

  C2 c2_1 (.B(B), .S(c2_1_s));
  // ADD16_LSB add16_lsb_1: pin names not known; wires that end beside it: A[15:0], S[15:0], c2_1_s[15:0], add16_lsb_1_p4
  // ADD16_MSB add16_msb_1: pin names not known; wires that end beside it: c2_1_s[31:16], A[31:16], 1'b0, add16_msb_1_p4, add16_msb_1_p5
  // ADD16_MSB add16_msb_2: pin names not known; wires that end beside it: c2_1_s[31:16], A[31:16], 1'b1, add16_msb_2_p4, add16_msb_2_p5
  LED led_1 (.in(add16_msb_1_p4));
  LED led_2 (.in(add16_msb_2_p4));
  Multiplexer #(.Bits(16)) multiplexer_1 (
    .sel(add16_lsb_1_p4), .in_0(add16_msb_1_p5), .in_1(add16_msb_2_p5), .out(S[31:16]));
endmodule
